# Fritzing sketch EsquemaCircuitos (saved by Fritzing 1.0.1rc)
breadboards: 1

parts:
  Mod1 = Raspberry Pi 4B
  DC_Mot_Enc1 = DC Motor with two-phase hall-encoder [part_number=VT-E-G25A-06-177E]
  DC_Mot_Enc2 = DC Motor with two-phase hall-encoder [part_number=VT-E-G25A-06-177E]
  PIR1 = PIR sensor
  GY1 = MPU-6050 Board GY-521 [form="♀ (female)" package=THT]
  Componente1 = Adafruit MAX98357A I2S 3W Class D Amplifier [part_number="Adafruit #3006"]
  Componente2 = Motor Driver 1A Dual TB6612FNG
  M1 = RPlidar A1M8 [package=THT]
  USBTTL1 = USB A Plug
  U2 = TCM8240MD [package=tcm8240md]
  USBTTL2 = USB A Plug
  U3 = LIPO-2000mAh [package=lipo-2000]
  USBTTL3 = Micro USB B Plug
  BAT1 = Battery Holders [package=lipo-1100mAh]
  SPKR1 = Loudspeaker
  Componente3 = Adafruit I2S Mic - SPH0645 [part_number="Adafruit #3421"]
  U4 = ESP32S-HiLetgo [part_number=ESP32S-HiLetgo]
  USBTTL4 = Micro USB B Plug

nets:
  N1: Mod1.3V3, DC_Mot_Enc1.pin2, DC_Mot_Enc2.pin2
  N2: Mod1.GPIO2, GY1.pin4
  N3: Mod1.GPIO3, GY1.pin3
  N4: Mod1.GPIO17, DC_Mot_Enc1.pin3
  N5: Mod1.GPIO18, Componente1.BCLK
  N6: Mod1.GPIO27, DC_Mot_Enc2.pin3
  GND: Mod1.GND, DC_Mot_Enc1.pin5, DC_Mot_Enc2.pin5, PIR1.GND, GY1.pin2, Componente1.GND, Componente2.GND, BAT1.-
  N7: Mod1.GPIO22, DC_Mot_Enc2.pin4
  N8: Mod1.GPIO24, PIR1.SIG
  N9: Mod1.GPIO25, DC_Mot_Enc1.pin4
  N10: Mod1.GPIO5, Componente2.STBY
  N11: Mod1.GPIO6, Componente2.BIN1
  N12: Mod1.GPIO12, Componente2.PWMA
  N13: Mod1.GPIO13, Componente2.PWMB
  N14: Mod1.GPIO19, Componente1.LRCLK
  N15: Mod1.GPIO16, Componente2.AIN1
  N16: Mod1.GPIO26, Componente2.BIN2
  N17: Mod1.GPIO20, Componente2.AIN2
  N18: Mod1.GPIO21, Componente1.DIN
  N19: DC_Mot_Enc1.pin1, Componente2.A02
  N20: DC_Mot_Enc1.pin6, Componente2.A01
  N21: DC_Mot_Enc2.pin1, Componente2.B01
  N22: DC_Mot_Enc2.pin6, Componente2.B02
  VDD: PIR1.VDD, GY1.pin1, Componente1.VIN, Componente2.VCC, BAT1.+
  N23: Componente1.VO-, SPKR1.pin1
  N24: Componente1.VO+, SPKR1.pin2
  N25: M1.pin1, M1.pin2, M1.pin3, M1.pin4, USBTTL1.usb
  N26: U2.DOUT7, U2.DOUT6, U2.DOUT5, U2.DOUT4, USBTTL2.usb
  N27: U3.+, U3.-, USBTTL3.usb, USBTTL4.usb
  N28: Componente3.VDD, U4.3.3
  GND_2: Componente3.GND, Componente3.SELECT, U4.GND
  N29: Componente3.BCLK, U4.GPIO21
  N30: Componente3.DATA, U4.GPIO22
  N31: Componente3.WS, U4.GPIO23

custom parts:
  MPU-6050 Board GY-521: Acelerometro y Giroscopio MPU-6050 Board GY-521
  Adafruit MAX98357A I2S 3W Class D Amplifier: Listen to this good news - we now have an all in one digital audio amp breakout board that works incredibly well with the Raspberry Pi! If you're looking for an easy and low cost way to get you digital sound files bumpin' then the MAX08357 I2S Amp Breakout is for you. It takes standard I2S digital audio input and, not only decodes it into analog, but also amplifies it directly into a speaker.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
  RPlidar A1M8: .The RPLIDAR A1 is the next generation low cost 360 degree 2D laser scanner (LIDAR) solution developed by SLAMTEC. It can take up to 4000 samples of laser ranging per second with high rotation speed. And equipped with SLAMTEC patented OPTMAG technology, it breakouts the life limitation of traditional LIDAR system so as to work stably for a long time.
  Adafruit I2S Mic - SPH0645: For many microcontrollers, adding audio input is easy with one of our analog microphone breakouts. But as you get to bigger and better microcontrollers and microcomputers, you'll find that you don't always have an analog input, or maybe you want to avoid the noise that can seep in with an analog mic system. Once you get past 8-bit micros, you will often find an I2S peripheral, that can take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
  ESP32S-HiLetgo: HiLetgo ESP-WROOM-32 ESP32 ESP-32S Development Board 2.4GHz Dual-Mode WiFi + Bluetooth Dual Cores Microcontroller The ESP32 integrated with Antenna switches, RF Balun, power amplifiers, low-noise amplifiers, filters, and management modules, and the entire solution occupies the least area of PCB. 2.4 GHz Wi-Fi plus Bluetooth dual-mode chip, with TSMC Ultra-low power consumption 40nm technology,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
